# Fritzing sketch esquema (saved by Fritzing 0.8.3b)
breadboards: 1

parts:
  LCD1 = LCD screen
  Part1 = Arduino Uno (Rev3)
  U1 = POT [package=pot_alpha_rv16af-20]

nets:
  N1: LCD1.RS, Part1.D7
  N2: LCD1.E, Part1.D8
  N3: LCD1.DB4, Part1.D9_PWM
  N4: LCD1.DB5, Part1.D10_PWM/SS
  N5: LCD1.DB6, Part1.ICSP_MOSI, Part1.D11_PWM/MOSI
  N6: LCD1.DB7, Part1.ICSP_MISO, Part1.D12/MISO
  N7: U1.A, U1.S, U1.E
